# Fritzing sketch Simdisplay (saved by Fritzing 0.9.3b)
breadboards: 2

parts:
  Part1 = Arduino Uno (Rev3)
  U1 = 74HC595 [package="DIP16 [THT]"]  # not connected
  U2 = 74HC595 [package="DIP16 [THT]"]
  R1 = Resistor [tolerance=±5% resistance=500 package="0603 [SMD]"]  # not connected
  R2 = Resistor [tolerance=±5% resistance=500 package="0603 [SMD]"]  # not connected
  R3 = Resistor [tolerance=±5% resistance=500 package="0603 [SMD]"]  # not connected
  R4 = Resistor [tolerance=±5% resistance=500 package="0603 [SMD]"]  # not connected
  R5 = Resistor [tolerance=±5% resistance=500 package="0603 [SMD]"]  # not connected
  R6 = Resistor [tolerance=±5% resistance=500 package="0603 [SMD]"]  # not connected
  R7 = Resistor [tolerance=±5% resistance=500 package="0603 [SMD]"]  # not connected
  R8 = Resistor [tolerance=±5% resistance=500 package="0603 [SMD]"]  # not connected
  U3 = 7-SEGMENT-DISPLAY [part_number=5161A6-1 package=7-segment-display]  # not connected
  R9 = Resistor [tolerance=±5% resistance=10k package="0603 [SMD]"]
  R10 = Resistor [tolerance=±5% resistance=10k package="0603 [SMD]"]
  R11 = Resistor [tolerance=±5% resistance=5k package="0603 [SMD]"]
  R12 = Resistor [tolerance=±5% resistance=10k package="0603 [SMD]"]
  R13 = Resistor [tolerance=±5% resistance=5k package="0603 [SMD]"]
  R14 = Resistor [tolerance=±5% resistance=5k package="0603 [SMD]"]
  R15 = Resistor [tolerance=±5% resistance=1k package="0603 [SMD]"]
  R16 = Resistor [tolerance=±5% resistance=1k package="0603 [SMD]"]
  LED3 = smd LED [color="Red (633nm)" package="1206 [SMD]"]  # not connected
  LED2 = smd LED [color="Red (633nm)" package="1206 [SMD]"]  # not connected
  LED1 = smd LED [color="Red (633nm)" package="1206 [SMD]"]  # not connected
  LED4 = smd LED [color="Red (633nm)" package="1206 [SMD]"]
  LED5 = smd LED [color="Red (633nm)" package="1206 [SMD]"]
  LED6 = smd LED [color="Red (633nm)" package="1206 [SMD]"]  # not connected
  LED7 = smd LED [color="Red (633nm)" package="1206 [SMD]"]
  LED8 = smd LED [color="Red (633nm)" package="1206 [SMD]"]
  LCD1 = LCD screen
  R17 = Rotary Potentiometer (Small) [maximum_resistance=10kΩ package=THT]
  R18 = Resistor [tolerance=±5% resistance=5k package=THT]

nets:
  N1: Part1.A0, LCD1.DB4
  N2: Part1.A1, LCD1.DB5
  N3: Part1.A2, LCD1.DB6
  N4: Part1.A3, LCD1.DB7
  N5: Part1.A4/SDA, LCD1.RS
  N6: Part1.A5/SCL, LCD1.E
  5V: Part1.5V, U2.MR, U2.VCC, LCD1.VDD, LCD1.LED+, R17.leg2
  GND: Part1.GND, R9.Pin_0, R10.Pin_0, R11.Pin_0, R12.Pin_0, R13.Pin_0, R14.Pin_0, R15.Pin_0, R16.Pin_0, LCD1.VSS, LCD1.R/W, R17.leg1, R18.Pin_1
  N7: R9.Pin_1, LED8.cathode
  N8: R10.Pin_1, LED7.cathode
  N9: R11.Pin_1, LED5.cathode
  N10: R13.Pin_1, LED4.cathode
  N11: LCD1.V0, R17.wiper
  N12: LCD1.LED-, R18.Pin_0
